# Fritzing sketch diagram (saved by Fritzing 0.9.10b)

parts:
  Part1 = Arduino Uno (Rev3)  # not connected
  Part2 = Arduino ProtoShield
  DS1 = DS18B20 1-Wire Temperature Sensor [part_number=DS18B20]

nets:
  5V: Part2.5V, DS1.VDD
  GND: Part2.GND, DS1.GND
  N1: Part2.D2, Part2.N$28
  N2: Part2.N$94, DS1.DQ
